// Logisim project Sum.circ as structural Verilog
module HalSum (
  input  a,
  input  b,
  output S,
  output C_out
);

  xor xor_1 (S, a, b);
  and and_1 (C_out, a, b);
endmodule

module FullSum (
  input  a,
  input  b,
  input  Ci,
  output S,
  output Co
);

  wire halsum_1_c_out, halsum_1_s, halsum_2_c_out;

  HalSum halsum_1 (.a(a), .b(b), .S(halsum_1_s), .C_out(halsum_1_c_out));
  HalSum halsum_2 (.a(halsum_1_s), .b(Ci), .S(S), .C_out(halsum_2_c_out));
  or or_1 (Co, halsum_2_c_out, halsum_1_c_out);
endmodule

module Sum (
  input  Carry_In,
  input  [3:0] a,
  input  [3:0] b,
  output Co,
  output [3:0] Saida
);

  wire fullsum_1_co, fullsum_2_co, fullsum_3_co;

  // Probe on a
  // Probe on b
  // Probe on Co
  // Probe on Saida
  FullSum fullsum_1 (.a(Carry_In), .b(b[0]), .Ci(a[0]), .S(Saida[0]), .Co(fullsum_1_co));
  FullSum fullsum_2 (.a(fullsum_1_co), .b(b[1]), .Ci(a[1]), .S(Saida[1]), .Co(fullsum_2_co));
  FullSum fullsum_3 (.a(fullsum_2_co), .b(b[2]), .Ci(a[2]), .S(Saida[2]), .Co(fullsum_3_co));
  FullSum fullsum_4 (.a(fullsum_3_co), .b(b[3]), .Ci(a[3]), .S(Saida[3]), .Co(Co));
endmodule
