// Logisim project ULA.circ as structural Verilog: 6 circuits, main circuit main
module main (
  input  in_1,
  input  [3:0] in_2,
  input  [3:0] in_3,
  input  [3:0] in_4,
  input  in_5,
  input  in_6,
  input  in_7,
  output [15:0] out_8
);

  wire [15:0] Reg_datab, ULA_resultado;

  Reg Reg (
    .Clock(in_5), .Enable(in_6), .Reset(in_7), .AddresA(in_2), .AddresB(in_3), .in_6(ULA_resultado),
    .DataA(out_8), .DataB(Reg_datab));
  // Probe on Reg_datab
  ULA ULA (.A(out_8), .B(Reg_datab), .Op(in_4), .Resultado(ULA_resultado));  // open: out_5
  // Probe on ULA_resultado
endmodule

module ULA (
  input  [15:0] A,
  input  [15:0] B,
  input  [3:0] Op,
  output [15:0] Resultado,
  output out_5
);

  wire [15:0] OutAnd, OutDiv, OutMul, OutNot, OutOr, OutShiLe, OutShiRi, OutSub, OutSum;

  Adder #(.width(16)) adder_1 (.a(A), .b(B), .out(OutSum));  // open: cin, cout
  Subtractor #(.width(16)) subtractor_1 (.a(A), .b(B), .out(OutSub));  // open: bin, bout
  Multiplier #(.width(16)) multiplier_1 (.a(A), .b(B), .out(OutMul));  // open: cin, cout
  Divider #(.width(16)) divider_1 (.a(A), .b(B), .out(OutDiv));  // open: upper, rem
  assign OutOr = A | B;  // OR_Gate or_1, 16 bits wide
  assign OutNot = ~A;  // NOT_Gate not_1, 16 bits wide
  assign OutAnd = A & B;  // AND_Gate and_1, 16 bits wide
  Shifter #(.width(16)) shifter_1 (.in(A), .\dist (B[3:0]), .out(OutShiLe));
  Shifter #(.width(16), .shift("lr")) shifter_2 (.in(A), .\dist (B[3:0]), .out(OutShiRi));
  Comparator #(.width(16)) comparator_1 (.a(A), .b(B), .gt(out_5));  // open: eq, lt
  Multiplexer #(.select(4), .width(16)) multiplexer_1 (
    .in0(OutSum), .in3(OutSub), .in6(OutMul), .in9(OutDiv), .in11(OutShiRi), .in12(OutOr), .in13(OutShiLe),
    .in14(OutAnd), .in15(OutNot), .out(Resultado), .sel(Op));  // open: in1, in2, in4, in5, in7, in8, in10, en
endmodule

module LatchSR (
  input  Set,
  input  Reset,
  output out_3
);

  wire and_1_out, and_2_out, not_2_out;

  and and_1 (and_1_out, Set, not_2_out);
  not not_1 (out_3, and_1_out);
  not not_2 (not_2_out, and_2_out);
  and and_2 (and_2_out, out_3, Reset);
endmodule

module LatchO (
  input  Data,
  input  Enabled,
  output out_3
);

  wire and_1_out, and_2_out, not_1_out, not_2_out, not_3_out;

  not not_1 (not_1_out, Data);
  and and_1 (and_1_out, Data, Enabled);
  and and_2 (and_2_out, Enabled, not_1_out);
  not not_2 (not_2_out, and_1_out);
  not not_3 (not_3_out, and_2_out);
  LatchSR latchsr_1 (.Set(not_2_out), .Reset(not_3_out), .out_3(out_3));
endmodule

module FlipFlop (
  input  D,
  input  Enabled,
  input  Clock,
  output out_4
);

  wire and_1_out, and_2_out, and_3_out, and_4_out, and_5_out, latchsr_1_out_3, not_1_out, not_2_out,
       not_3_out, not_4_out, not_5_out, not_6_out, not_7_out;

  and and_1 (and_1_out, Enabled, Clock);
  not not_1 (not_1_out, D);
  not not_2 (not_2_out, Clock);
  and and_2 (and_2_out, D, and_1_out);
  and and_3 (and_3_out, and_1_out, not_1_out);
  not not_3 (not_3_out, and_2_out);
  not not_4 (not_4_out, and_3_out);
  LatchSR latchsr_1 (.Set(not_3_out), .Reset(not_4_out), .out_3(latchsr_1_out_3));
  not not_5 (not_5_out, latchsr_1_out_3);
  and and_4 (and_4_out, latchsr_1_out_3, not_2_out);
  not not_6 (not_6_out, and_4_out);
  and and_5 (and_5_out, not_2_out, not_5_out);
  not not_7 (not_7_out, and_5_out);
  LatchSR latchsr_2 (.Set(not_6_out), .Reset(not_7_out), .out_3(out_4));
endmodule

module Reg (
  input  Clock,
  input  Enable,
  input  Reset,
  input  [3:0] AddresA,
  input  [3:0] AddresB,
  input  [15:0] in_6,
  output [15:0] DataA,
  output [15:0] DataB
);

  wire en0, en1, en2, en3, en4, en5, en6, en7, en8, en9, en10, en11, en12, en13, en14, en15;
  wire [15:0] out0, out1, out2, out3, out4, out5, out6, out7, out8, out9, out10, out11, out12, out13, out14,
       out15;

  Demultiplexer #(.select(4)) demultiplexer_1 (
    .out0(en0), .out1(en1), .out2(en2), .out3(en3), .out4(en4), .out5(en5), .out6(en6), .out7(en7),
    .out8(en8), .out9(en9), .out10(en10), .out11(en11), .out12(en12), .out13(en13), .out14(en14),
    .out15(en15), .in(Enable), .sel(AddresA));  // open: en
  Register #(.width(16)) register_1 (.D(in_6), .en(en0), .Q(out0), .clk(Clock), .clr(Reset));
  Register #(.width(16)) register_2 (.D(in_6), .en(en4), .Q(out4), .clk(Clock), .clr(Reset));
  Register #(.width(16)) register_3 (.D(in_6), .en(en8), .Q(out8), .clk(Clock), .clr(Reset));
  Register #(.width(16)) register_4 (.D(in_6), .en(en12), .Q(out12), .clk(Clock), .clr(Reset));
  Register #(.width(16)) register_5 (.D(in_6), .en(Enable), .Q(out1), .clk(Clock), .clr(Reset));
  Register #(.width(16)) register_6 (.D(in_6), .en(en5), .Q(out5), .clk(Clock), .clr(Reset));
  Register #(.width(16)) register_7 (.D(in_6), .en(en9), .Q(out9), .clk(Clock), .clr(Reset));
  Register #(.width(16)) register_8 (.D(in_6), .en(en13), .Q(out13), .clk(Clock), .clr(Reset));
  Register #(.width(16)) register_9 (.D(in_6), .en(en2), .Q(out2), .clk(Clock), .clr(Reset));
  Register #(.width(16)) register_10 (.D(in_6), .en(en6), .Q(out6), .clk(Clock), .clr(Reset));
  Register #(.width(16)) register_11 (.D(in_6), .en(en10), .Q(out10), .clk(Clock), .clr(Reset));
  Register #(.width(16)) register_12 (.D(in_6), .en(en14), .Q(out14), .clk(Clock), .clr(Reset));
  Register #(.width(16)) register_13 (.D(in_6), .en(en3), .Q(out3), .clk(Clock), .clr(Reset));
  Register #(.width(16)) register_14 (.D(in_6), .en(en7), .Q(out7), .clk(Clock), .clr(Reset));
  Register #(.width(16)) register_15 (.D(in_6), .en(en11), .Q(out11), .clk(Clock), .clr(Reset));
  Register #(.width(16)) register_16 (.D(in_6), .en(en15), .Q(out15), .clk(Clock), .clr(Reset));
  Multiplexer #(.select(4), .width(16)) multiplexer_1 (
    .in0(out0), .in1(out1), .in2(out2), .in3(out3), .in4(out4), .in5(out5), .in6(out6), .in7(out7),
    .in8(out8), .in9(out9), .in10(out10), .in11(out11), .in12(out12), .in13(out13), .in14(out14),
    .in15(out15), .out(DataA), .sel(AddresA));  // open: en
  Multiplexer #(.select(4), .width(16)) multiplexer_2 (
    .in0(out0), .in1(out1), .in2(out2), .in3(out3), .in4(out4), .in5(out5), .in6(out6), .in7(out7),
    .in8(out8), .in9(out9), .in10(out10), .in11(out11), .in12(out12), .in13(out13), .in14(out14),
    .in15(out15), .out(DataB), .sel(AddresB));  // open: en

  // Other names for the same wires on the sheet: addA[3:0] = AddresA; addB[3:0] = AddresB; clk = Clock;
  //   data[15:0] = in_6; en = Enable; rst = Reset
endmodule
